# Fritzing sketch LumiMonitor_MotionSensor (saved by Fritzing 0.9.3b)
circuit board: 3.11052cm x 3.38888cm
breadboards: 1

parts:
  Raspberry_Pi_1 = Raspberry Pi 3 [part_number=RPI-3-V1.2]
  PIR_Motion_Sensor = Grove Light Sensor

nets:
  N1: Raspberry_Pi_1.GPIO18, PIR_Motion_Sensor.SIG
  GND: Raspberry_Pi_1.GND, PIR_Motion_Sensor.GND
  5V: Raspberry_Pi_1.5V, PIR_Motion_Sensor.VCC

notes:
  Kyle Voduris
  N01246531
  D1
  NC
  VCC
  GND

custom parts:
  Grove Light Sensor: An analog light sensor
