# Fritzing sketch LumiMonitor_MotionSensor2 (saved by Fritzing 0.9.3b)
circuit board: 2.20501cm x 3.0155cm
breadboards: 1

parts:
  J1 = female pin header, 3 pins [form="♀ (female)"]
  PIR_Motion_Sensor = Grove Light Sensor

nets:
  N1: J1.pin1, PIR_Motion_Sensor.GND
  N2: J1.pin2, PIR_Motion_Sensor.VCC
  N3: J1.pin3, PIR_Motion_Sensor.SIG

notes:
  Kyle Voduris
  D1
  NC
  VCC
  GND
  N01246531

custom parts:
  Grove Light Sensor: An analog light sensor
